# Fritzing sketch radio_rx (saved by Fritzing 1.0.0rc)
breadboards: 1

parts:
  U2 = XD-RF-5V [package=THT]
  IC1 = L293D mini motor shield [package=THT]
  Part1 = Arduino Uno (Rev3) - ICSP

nets:
  VCC: U2.VCC, IC1.VCC, Part1.5V
  N1: U2.DATA, Part1.D11_PWM/MOSI
  GND: U2.GND, IC1.GND, Part1.GND
  VIN: IC1.VIN, Part1.VIN
  N2: IC1.B1-, IC1.IN4, Part1.D7
  N3: IC1.IN1, Part1.D4
  N4: IC1.IN2, Part1.D5_PWM
  N5: IC1.IN3, Part1.D6_PWM

custom parts:
  XD-RF-5V: This is 433Mhz RF transmitter with receiver kit for Arduino ARM MCU wireless Application environment: Remote control switch, receiver module, motorcycles, automobile anti-theft products, home security products, electric doors, shutter doors, windows, remote control socket, remote control LED, remote audio remote control electric doors, garage door remote control, remote control retractable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
  L293D mini motor shield: L293D Motor Driver
