# Fritzing sketch radio_tx (saved by Fritzing 1.0.0rc)
breadboards: 1

parts:
  Part1 = Arduino Uno (Rev3) - ICSP
  U1 = FS1000A - 433Mhz RF Transmitter [package=THT]
  Part3 = KY-023 Dual Axis Joystick Module [package="Breakout board"]

nets:
  N1: Part1.A0, Part3.VRx
  N2: Part1.A1, Part3.VRy
  5V: Part1.5V, U1.DATA, Part3.+5V
  N3: Part1.D12/MISO, U1.VCC
  GND: Part1.GND, U1.GND, Part3.GND

custom parts:
  FS1000A - 433Mhz RF Transmitter: This is 433Mhz RF transmitter with receiver kit for Arduino ARM MCU wireless Application environment: Remote control switch, receiver module, motorcycles, automobile anti-theft products, home security products, electric doors, shutter doors, windows, remote control socket, remote control LED, remote audio remote control electric doors, garage door remote control, remote control retractable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
  KY-023 Dual Axis Joystick Module: X/Y Analog Joystick KEYES KY-023 module. It contains two potentiometers and a button.
